// Logisim project BOL1.circ as structural Verilog: 1 circuit, main circuit main
module main (
  input  A,
  input  B,
  input  C,
  input  D
);

  wire and_1_out, and_2_out, and_3_out, not_1_out, not_2_out, not_3_out, not_4_out, or_1_out, undriven,
       undriven_2, undriven_3, undriven_4;

  not not_1 (not_1_out, undriven_3);
  and and_1 (and_1_out, not_1_out, not_2_out, undriven_4);
  not not_2 (not_2_out, undriven_2);
  not not_3 (not_3_out, undriven);
  not not_4 (not_4_out, D);
  and and_2 (and_2_out, not_3_out, C, not_4_out);
  or or_1 (or_1_out, and_3_out, and_2_out, and_1_out);
  and and_3 (and_3_out, A, B);
  LED led_1 (.in(or_1_out));
endmodule
