// Logisim project 3boletin1.2 nor corregido.circ as structural Verilog: 1 circuit, main circuit main
module main (
  input  A,
  input  B,
  input  C,
  input  D,
  input  A_2,
  input  B_2,
  input  C_2,
  input  D_2,
  output out_9
);

  wire nor_1_out, nor_2_out, nor_3_out, nor_4_out, nor_5_out, nor_6_out;

  nor nor_1 (nor_1_out, ~A, ~B);  // NOR_Gate
  nor nor_2 (nor_2_out, ~A, ~C);  // NOR_Gate
  nor nor_3 (nor_3_out, ~A_2, ~B_2);  // NOR_Gate
  nor nor_4 (nor_4_out, ~A_2, ~C_2);  // NOR_Gate
  nor nor_5 (nor_5_out, nor_1_out, nor_2_out);
  nor nor_6 (nor_6_out, nor_3_out, nor_4_out);
  nor nor_7 (out_9, nor_5_out, nor_6_out);
endmodule
