// Logisim project a,b,c,d final(1boletin).circ as structural Verilog: 5 circuits, main circuit c
module c (
  input  A,
  input  B,
  input  C,
  input  D,
  output out_5
);

  wire and_1_out, and_2_out, and_3_out;

  and and_1 (and_1_out, A, B);
  and and_2 (and_2_out, ~B, C, ~D);  // AND_Gate
  and and_3 (and_3_out, ~C, ~B, D);  // AND_Gate
  or or_1 (out_5, and_1_out, and_2_out, and_3_out);
endmodule

module D (
  input  A,
  input  B,
  input  C,
  input  in_4,
  output out_5
);

  wire and_1_out, and_2_out, and_3_out;

  and and_1 (and_1_out, B, C);
  and and_2 (and_2_out, B, in_4);
  and and_3 (and_3_out, C, in_4);
  or or_1 (out_5, and_1_out, and_2_out, and_3_out);
endmodule

module a (
  input  a,
  input  b,
  input  c,
  input  d,
  output out_5
);

  wire and_1_out, and_2_out, and_3_out;

  and and_1 (and_1_out, ~a, ~b, c);  // AND_Gate
  and and_2 (and_2_out, ~a, b, ~c);  // AND_Gate
  and and_3 (and_3_out, a, ~b, ~c);  // AND_Gate
  or or_1 (out_5, and_1_out, and_2_out, and_3_out);
endmodule

module \union  (
  input  A,
  input  B,
  input  C,
  input  D
);

  wire a_1_out_5, b_1_out_5, c_1_out_5, d_1_out_5;

  LED led_1 (.in(a_1_out_5));
  a a_1 (.a(A), .b(B), .c(C), .d(D), .out_5(a_1_out_5));
  LED led_2 (.in(b_1_out_5));
  b b_1 (.a(A), .b(B), .c(C), .d(D), .out_5(b_1_out_5));
  LED led_3 (.in(c_1_out_5));
  c c_1 (.A(A), .B(B), .C(C), .D(D), .out_5(c_1_out_5));
  D d_1 (.A(A), .B(B), .C(C), .in_4(D), .out_5(d_1_out_5));
  LED led_4 (.in(d_1_out_5));
endmodule

module b (
  input  a,
  input  b,
  input  c,
  input  d,
  output out_5
);

  wire and_1_out, and_2_out, and_3_out;

  and and_1 (and_1_out, ~a, b, ~c, ~d);  // AND_Gate
  and and_2 (and_2_out, ~b, d);  // AND_Gate
  and and_3 (and_3_out, a, c);
  or or_1 (out_5, and_1_out, and_2_out, and_3_out);
endmodule
