// Logisim project cosa.circ as structural Verilog: 1 circuit, main circuit main
module main (
  input  i0,
  input  i1,
  input  i2,
  input  i3,
  output out_5,
  output out_6
);

  wire and_1_out, and_2_out, not_2_out, not_3_out, not_4_out;

  // NOT_Gate not_1 has open pins: in=i0, out=open
  not not_2 (not_2_out, i1);
  not not_3 (not_3_out, i2);
  not not_4 (not_4_out, i3);
  and and_1 (and_1_out, not_3_out, i3);
  and and_2 (and_2_out, i3, i2, not_2_out);
  or or_1 (out_6, and_2_out, not_4_out);
  or or_2 (out_5, and_1_out, not_4_out);
endmodule
