// Logisim project contador asincrono.circ as structural Verilog: 1 circuit, main circuit main
module main (
  input  in_1,
  input  in_2,
  output [2:0] out_3
);

  wire and_1_out, clock_1_out, j_k_ff_1_qn, j_k_ff_2_qn, or_1_out;

  Clock clock_1 (.out(clock_1_out));
  or or_1 (or_1_out, in_2, and_1_out);
  J_K_Flip_Flop j_k_ff_1 (
    .J(1'b1), .clk(clock_1_out), .K(1'b1), .Q(out_3[0]), .Qn(j_k_ff_1_qn), .preset(in_1), .reset(or_1_out));  // open: en
  J_K_Flip_Flop j_k_ff_2 (
    .J(1'b1), .clk(j_k_ff_1_qn), .K(1'b1), .Q(out_3[1]), .Qn(j_k_ff_2_qn), .preset(in_1), .reset(or_1_out));  // open: en
  J_K_Flip_Flop j_k_ff_3 (
    .J(1'b1), .clk(j_k_ff_2_qn), .K(1'b1), .Q(out_3[2]), .preset(in_1), .reset(or_1_out));  // open: Qn, en
  and and_1 (and_1_out, out_3[0], ~out_3[1], out_3[2]);  // AND_Gate
endmodule
