// Logisim project main.c.circ as structural Verilog: 1 circuit, main circuit main
module main (
  output [2:0] out_1
);

  wire and_1_out, and_2_out, and_3_out, and_4_out, clock_1_out, t_ff_1_q, undriven;

  Clock clock_1 (.out(clock_1_out));
  T_Flip_Flop t_ff_1 (.clk(clock_1_out), .T(1'b1), .Q(t_ff_1_q), .preset(and_3_out));  // open: Qn, reset, en
  T_Flip_Flop t_ff_2 (.clk(t_ff_1_q), .T(1'b1), .Q(out_1[1]), .reset(and_3_out));  // open: Qn, preset, en
  or or_1 (out_1[0], and_4_out, and_2_out, and_1_out);
  and and_1 (and_1_out, out_1[1], t_ff_1_q);
  and and_2 (and_2_out, t_ff_1_q, ~out_1[2]);  // AND_Gate
  T_Flip_Flop t_ff_3 (.clk(out_1[1]), .T(1'b1), .Q(out_1[2]), .reset(undriven));  // open: Qn, preset, en
  and and_3 (and_3_out, ~t_ff_1_q, out_1[1], ~out_1[2]);  // AND_Gate
  and and_4 (and_4_out, out_1[2], ~out_1[1], ~t_ff_1_q);  // AND_Gate

  // Notes on the sheet:
  //   Q0
  //   Q1
  //   Q2
endmodule
