// Logisim project main.circ as structural Verilog: 1 circuit, main circuit main
module main (
);

  wire and_1_out, clock_1_out, j_k_ff_1_qn, j_k_ff_2_qn, not_1_out, not_2_out, not_3_out, not_4_out;
  wire [2:0] j_k_ff_1_q;

  Clock clock_1 (.out(clock_1_out));
  J_K_Flip_Flop j_k_ff_1 (
    .J(1'b1), .clk(clock_1_out), .K(1'b1), .Q(j_k_ff_1_q[0]), .Qn(j_k_ff_1_qn), .reset(not_1_out));  // open: preset, en
  not not_1 (not_1_out, not_3_out);
  and and_1 (and_1_out, j_k_ff_1_q[0], j_k_ff_2_qn, j_k_ff_1_q[2]);
  J_K_Flip_Flop j_k_ff_2 (
    .J(1'b1), .clk(j_k_ff_1_qn), .K(1'b1), .Q(j_k_ff_1_q[1]), .Qn(j_k_ff_2_qn), .reset(not_2_out));  // open: preset, en
  not not_2 (not_2_out, not_3_out);
  not not_3 (not_3_out, and_1_out);
  Hex_Digit_Display hex_digit_display_1 (.value({1'b0, j_k_ff_1_q}));  // open: dp
  J_K_Flip_Flop j_k_ff_3 (
    .J(1'b1), .clk(j_k_ff_2_qn), .K(1'b1), .Q(j_k_ff_1_q[2]), .reset(not_4_out));  // open: Qn, preset, en
  not not_4 (not_4_out, not_3_out);
endmodule
