// Logisim project main.circ as structural Verilog: 1 circuit, main circuit main
module main (
  input  [1:0] in_1,
  output out_2
);

  wire _1Q_q, and_1_out, clock_1_out, not_1_out, not_2_out, not_3_out, Q0_q;

  Clock clock_1 (.out(clock_1_out));
  not not_1 (not_1_out, in_1[0]);
  not not_2 (not_2_out, in_1[1]);
  not not_3 (not_3_out, in_1[0]);
  and and_1 (and_1_out, in_1[1], not_1_out, _1Q_q);
  D_Flip_Flop Q0 (.clk(clock_1_out), .D(and_1_out), .Q(Q0_q));  // open: Qn, preset, en, reset
  D_Flip_Flop _1Q (.clk(clock_1_out), .D(not_2_out), .Q(_1Q_q));  // open: Qn, preset, en, reset
  and and_2 (out_2, Q0_q, not_3_out, in_1[1]);

  // Notes on the sheet:
  //   O-->11
  //   Entradas:
  //   N--> 00
  //   S--> 01
  //   E-->10
endmodule
