// Logisim project main.circ as structural Verilog: 1 circuit, main circuit main
module main (
  input  [3:0] in_1,
  input  [3:0] in_2,
  output [3:0] out_3,
  output out_4
);

  wire and_2_out, and_3_out, comparator_1_gt, or_1_out, xor_1_out;
  wire [3:0] multiplexer_1_out;

  // AND_Gate and_1 is placed but not wired
  xor xor_1 (xor_1_out, in_1[3], in_2[3]);
  Comparator #(.width(4), .mode("unsigned")) comparator_1 (.a(in_1), .b(in_2), .gt(comparator_1_gt));  // open: eq, lt
  and and_2 (and_2_out, xor_1_out, ~comparator_1_gt);  // AND_Gate
  and and_3 (and_3_out, comparator_1_gt, ~xor_1_out);  // AND_Gate
  Multiplexer #(.width(4)) multiplexer_1 (.in0(in_2), .in1(in_1), .out(multiplexer_1_out), .sel(or_1_out));  // open: en
  or or_1 (or_1_out, and_2_out, and_3_out);
  Adder #(.width(4)) adder_1 (.a(4'b0001), .b(multiplexer_1_out), .out(out_3), .cout(out_4));  // open: cin
endmodule
