// Logisim project main1.circ as structural Verilog: 1 circuit, main circuit main
module main (
  output [3:0] out_1
);

  wire _0_qn, _1_q, _1_qn, _2_q, _2_qn, and_1_out, and_2_out, and_3_out, and_4_out, and_5_out, and_6_out,
       clock_1_out;

  Clock clock_1 (.out(clock_1_out));
  and and_1 (and_1_out, _1_q, out_1[1]);
  and and_2 (and_2_out, _2_q, _1_qn, _0_qn);
  and and_3 (and_3_out, _2_qn, _1_qn, out_1[1]);
  and and_4 (and_4_out, _1_q, _0_qn);
  and and_5 (and_5_out, _2_qn, out_1[1]);
  and and_6 (and_6_out, _2_qn, out_1[1]);
  or or_1 (out_1[2], and_2_out, and_3_out, and_4_out);
  J_K_Flip_Flop _2 (.J(and_1_out), .clk(clock_1_out), .K(out_1[1]), .Q(_2_q), .Qn(_2_qn));  // open: preset, en, reset
  J_K_Flip_Flop _1 (.J(and_6_out), .clk(clock_1_out), .K(out_1[1]), .Q(_1_q), .Qn(_1_qn));  // open: preset, en, reset
  J_K_Flip_Flop _0 (.J(1'b1), .clk(clock_1_out), .K(out_1[1]), .Q(out_1[1]), .Qn(_0_qn));  // open: preset, en, reset
  or or_2 (out_1[0], and_5_out, _1_q);
  _7_Segment_Display u_7_segment_display_1 ();  // open: g, f, a, b, e, d, c, dp
  Hex_Digit_Display hex_digit_display_1 (.value({1'b0, out_1[2:0]}));  // open: dp

  assign out_1[3] = 1'b0;

  // Notes on the sheet:
  //   Q1
  //   Q2
  //   Q0
endmodule
