// Logisim project 6.circ as structural Verilog: 3 circuits, main circuit Unidades
module Unidades (
  input  CLK,
  input  RESET,
  output Q3,
  output Q2,
  output Q1,
  output Q0
);

  wire and_1_out, and_2_out, and_3_out, and_4_out, and_5_out, and_6_out, and_7_out, not_1_out, or_1_out,
       or_2_out, or_3_out;

  not not_1 (not_1_out, Q0);
  and and_1 (and_1_out, Q2, Q1, Q0);
  and and_2 (and_2_out, Q3, ~Q0);  // AND_Gate
  and and_3 (and_3_out, Q2, ~Q0);  // AND_Gate
  and and_4 (and_4_out, Q2, ~Q1);  // AND_Gate
  and and_5 (and_5_out, ~Q2, Q1, Q0);  // AND_Gate
  and and_6 (and_6_out, ~Q3, ~Q1, Q0);  // AND_Gate
  and and_7 (and_7_out, Q1, ~Q0);  // AND_Gate
  or or_1 (or_1_out, and_6_out, and_7_out);
  or or_2 (or_2_out, and_1_out, and_2_out);
  or or_3 (or_3_out, and_3_out, and_4_out, and_5_out);
  D_Flip_Flop d_ff_1 (.clk(CLK), .D(or_2_out), .Q(Q3), .reset(RESET));  // open: Qn, preset, en
  D_Flip_Flop d_ff_2 (.clk(CLK), .D(or_3_out), .Q(Q2), .reset(RESET));  // open: Qn, preset, en
  D_Flip_Flop d_ff_3 (.clk(CLK), .D(or_1_out), .Q(Q1), .reset(RESET));  // open: Qn, preset, en
  D_Flip_Flop d_ff_4 (.clk(CLK), .D(not_1_out), .Q(Q0), .reset(RESET));  // open: Qn, preset, en
endmodule

module Principal (
);

  wire clock_1_out, Decenas, undriven;
  wire [2:0] decenas_1_q0;
  wire [3:0] unidades_1_q0;

  Clock clock_1 (.out(clock_1_out));
  Hex_Digit_Display hex_digit_display_1 (.value({1'b0, decenas_1_q0}));  // open: dp
  decenas decenas_1 (.CLK(Decenas), .Q2(decenas_1_q0[2]), .Q1(decenas_1_q0[1]), .Q0(decenas_1_q0[0]));  // open: RESET
  Hex_Digit_Display hex_digit_display_2 (.value(unidades_1_q0), .dp(undriven));
  Unidades unidades_1 (
    .CLK(clock_1_out), .Q3(unidades_1_q0[3]), .Q2(unidades_1_q0[2]), .Q1(unidades_1_q0[1]),
    .Q0(unidades_1_q0[0]));  // open: RESET
  and and_1 (Decenas, ~unidades_1_q0[3], ~unidades_1_q0[2], ~unidades_1_q0[1], ~unidades_1_q0[0]);  // AND_Gate
endmodule

module decenas (
  input  CLK,
  input  RESET,
  output Q2,
  output Q1,
  output Q0
);

  wire and_1_out, and_2_out, and_3_out, and_4_out, not_1_out, or_1_out, or_2_out;

  and and_1 (and_1_out, ~Q2, Q1, Q0);  // AND_Gate
  and and_2 (and_2_out, Q2, ~Q0);  // AND_Gate
  not not_1 (not_1_out, Q0);
  and and_3 (and_3_out, ~Q2, ~Q1, Q0);  // AND_Gate
  and and_4 (and_4_out, Q1, ~Q0);  // AND_Gate
  or or_1 (or_1_out, and_1_out, and_2_out);
  or or_2 (or_2_out, and_3_out, and_4_out);
  D_Flip_Flop d_ff_1 (.clk(CLK), .D(or_1_out), .Q(Q2), .reset(RESET));  // open: Qn, preset, en
  D_Flip_Flop d_ff_2 (.clk(CLK), .D(or_2_out), .Q(Q1), .reset(RESET));  // open: Qn, preset, en
  D_Flip_Flop d_ff_3 (.clk(CLK), .D(not_1_out), .Q(Q0), .reset(RESET));  // open: Qn, preset, en
endmodule
