// Logisim project 5.circ as structural Verilog: 1 circuit, main circuit main
module main (
  input  A,
  input  D,
  input  t1,
  input  t0,
  output E,
  output C
);

  wire and_1_out, nor_1_out, or_1_out, or_2_out;

  and and_1 (and_1_out, ~A, D);  // AND_Gate
  or or_1 (or_1_out, ~A, D);  // OR_Gate
  or or_2 (or_2_out, and_1_out, ~t0);  // OR_Gate
  nor nor_1 (nor_1_out, t1, t0);
  and and_2 (E, or_2_out, t1);
  and and_3 (C, nor_1_out, or_1_out);
endmodule
