// Logisim project 3.circ as structural Verilog: 2 circuits, main circuit main
module main (
  input  A,
  input  B,
  input  C,
  input  D,
  output out_5
);

  wire or_1_out;

  or or_1 (or_1_out, B, C, C);
  and and_1 (out_5, A, or_1_out);
endmodule

module _3 (
  input  in_1,
  input  in_2,
  input  in_3,
  input  in_4,
  input  in_5,
  input  in_6,
  input  in_7,
  input  in_8,
  output out_9
);

  wire main_1_out_5, main_2_out_5;

  main main_1 (.A(in_1), .B(in_2), .C(in_3), .D(in_4), .out_5(main_1_out_5));
  main main_2 (.A(in_5), .B(in_6), .C(in_7), .D(in_8), .out_5(main_2_out_5));
  or or_1 (out_9, main_1_out_5, main_2_out_5);
endmodule
