// Logisim project 4boletin1.circ as structural Verilog: 1 circuit, main circuit main
module main (
  input  E,
  input  s1,
  input  s2,
  output M1,
  output M2
);

  wire and_1_out, and_2_out;

  and and_1 (and_1_out, E, s1, s2);
  and and_2 (and_2_out, E, s1, ~s2);  // AND_Gate
  or or_1 (M1, and_1_out, and_2_out);
  and and_3 (M2, E, s1, s2);
endmodule
