// Logisim project 4boletin1bien.circ as structural Verilog: 2 circuits, main circuit main
module main (
  input  E,
  input  s1,
  input  s2,
  output M1,
  output M2
);

  and and_1 (M1, E, s1);
  and and_2 (M2, E, s2);
endmodule

module \nor  (
  input  E,
  input  s1,
  input  s2,
  output M1,
  output M2
);

  wire nor_1_out, nor_2_out, nor_3_out;

  nor nor_1 (nor_1_out, E, E);
  nor nor_2 (nor_2_out, s1, s1);
  nor nor_3 (nor_3_out, s2, s2);
  nor nor_4 (M1, nor_1_out, nor_2_out);
  nor nor_5 (M2, nor_1_out, nor_3_out);
endmodule
