// Logisim project contador.circ as structural Verilog: 1 circuit, main circuit main
module main (
  output [2:0] out_1
);

  wire and_1_out, clock_1_out, not_1_out, not_2_out, or_1_out;

  Clock clock_1 (.out(clock_1_out));
  or or_1 (or_1_out, out_1[0], ~out_1[1]);  // OR_Gate
  not not_1 (not_1_out, out_1[1]);
  not not_2 (not_2_out, out_1[2]);
  and and_1 (and_1_out, not_1_out, not_2_out);
  J_K_Flip_Flop Q2 (.J(or_1_out), .clk(clock_1_out), .K(not_1_out), .Q(out_1[2]));  // open: Qn, preset, en, reset
  J_K_Flip_Flop Q1 (.J(1'b1), .clk(clock_1_out), .K(1'b1), .Q(out_1[1]));  // open: Qn, preset, en, reset
  J_K_Flip_Flop Q0 (.J(and_1_out), .clk(clock_1_out), .K(not_2_out), .Q(out_1[0]));  // open: Qn, preset, en, reset

  // Other names for the same wires on the sheet: _0 = out_1[0]; _1 = out_1[1]; _2 = out_1[2]
endmodule
